# Fritzing sketch Gelatiera_III_for_schematic (saved by Fritzing 0.9.4)

parts:
  Part2 = Adafruit LM4040 Voltage Reference [part_number="Adafruit #2200"]
  Part3 = Adafruit 1.44 inch TFT Breakout [part_number="Adafruit #2088"]
  Part4 = OLED Monochrome 128x64 1.3 inch [part_number=938]
  M1 = DRV8834
  M2 = Stepper Motor - Bipolar
  Power_supply_(9V_5_A) = Power plug
  Peltier1 = Peltier Element
  Peltier2 = Peltier Element
  Part10 = Arduino Mega ADK (Rev3)
  Power_supply_(19_V_16_A) = Power plug
  MD03A4 = Pololu VNH5019 v8 [part_number=MD03A]
  Buzzer = Piezo Speaker
  R1 = Resistor [tolerance=±5% resistance=30.11k package=THT]
  R2 = Resistor [tolerance=±5% resistance=30.11k package=THT]
  R3 = Resistor [tolerance=±5% resistance=30.11k package=THT]
  R4 = Resistor [tolerance=±5% resistance=30.11k package=THT]
  C3 = Ceramic Capacitor [capacitance=1µF package="100 mil [THT, multilayer]"]
  C4 = Ceramic Capacitor [capacitance=1µF package="100 mil [THT, multilayer]"]
  C5 = Ceramic Capacitor [capacitance=1µF package="100 mil [THT, multilayer]"]
  C6 = Ceramic Capacitor [capacitance=1µF package="100 mil [THT, multilayer]"]
  Thermistor3 = Temperature Sensor (Thermistor) [thermistor_type=NTC package=THT]
  Thermistor2 = Temperature Sensor (Thermistor) [thermistor_type=NTC package=THT]
  Thermistor1 = Temperature Sensor (Thermistor) [thermistor_type=NTC package=THT]
  Power_switch = Toggle Switch [package=THT]
  C7 = Ceramic Capacitor [capacitance=0.1mF package="100 mil [THT, multilayer]"]
  S3 = SWITCH-MOMENTARY-2 [package=tactile_switch_smd-2]
  S4 = SWITCH-MOMENTARY-2 [package=tactile_switch_smd-2]
  R8 = Resistor [tolerance=±5% resistance=10k package=THT]
  R9 = Resistor [tolerance=±5% resistance=100 package=THT]
  R10 = Resistor [tolerance=±5% resistance=100 package=THT]
  R11 = Resistor [tolerance=±5% resistance=100 package=THT]
  R12 = Resistor [tolerance=±5% resistance=100 package=THT]
  R13 = Resistor [tolerance=±5% resistance=100 package=THT]
  R14 = Resistor [tolerance=±5% resistance=100 package=THT]
  Part5 = Adafruit ADS1115 16Bit I2C ADC [part_number="Adafruit #1085"]
  S5 = JOYSTICK_10mm_2 [package=SMD]

nets (from the schematic view):
  VIN: Part2.VIN, Part3.VIN, Part4.VIN, Part10.IOREF, Part10.5V, MD03A4.VDD, S3.1, S4.1, S5.pin_1
  GND: Part2.GND, Part3.GND, Part4.GND, M1.Pin_9, M1.Pin_15, Power_supply_(9V_5_A).GND, Part10.GND, MD03A4.GND#135, Buzzer.pin1, C3.0, C4.0, C5.0, C6.0, Thermistor3.pin_1, Thermistor2.pin_1, Thermistor1.pin_1, C7.1, R8.Pin_1, R9.Pin_1, R10.Pin_1, R11.Pin_1, R12.Pin_1, R13.Pin_1, R14.Pin_1, Part5.GND
  N1: Part2.2.048V, R1.Pin_1, R2.Pin_1, R3.Pin_1, R4.Pin_1
  N2: Part2.4.096V, Part5.VDD
  N3: Part3.SCK, Part4.SCLK_SCK, Part10.D52/SCK
  N4: Part3.MISO, Part10.D50/MISO
  N5: Part3.MOSI, Part4.MOSI_SDA, Part10.D51/MOSI
  N6: Part3.TFTCS, Part10.D41
  N7: Part3.TFTDC, Part10.D38
  N8: Part3.CARDCS, Part10.D40
  N9: Part4.DC_SA0, Part10.D42
  N10: Part4.CS, Part10.D43
  N11: M1.Pin_2, Part10.D24
  N12: M1.Pin_3, Part10.D25
  N13: M1.Pin_6, Part10.D26
  N14: M1.Pin_7, Part10.D23
  N15: M1.Pin_8, Part10.D22
  N16: M1.Pin_11, M2.D
  N17: M1.Pin_12, M2.B
  N18: M1.Pin_13, M2.C
  N19: M1.Pin_14, M2.A
  N20: M1.Pin_16, Power_supply_(9V_5_A).VCC, Power_switch.COM, C7.0
  N21: Peltier1.pin1, MD03A4.M1A
  N22: Peltier1.pin2, MD03A4.M1B
  N23: Peltier2.pin1, MD03A4.M2A
  N24: Peltier2.pin2, MD03A4.M2B
  N25: Part10.D21/SCL, Part5.SCL
  N26: Part10.D20/SDA, Part5.SDA
  N27: Part10.D12_PWM, Buzzer.pin2
  N28: Part10.D11_PWM, MD03A4.M2PWM
  N29: Part10.D10_PWM, MD03A4.M2EN
  N30: Part10.D9_PWM, MD03A4.M2INB
  N31: Part10.D8_PWM, MD03A4.M2INA
  N32: Part10.VIN, Power_switch.L2
  N33: Part10.D4_PWM, MD03A4.M1INA
  N34: Part10.D5_PWM, MD03A4.M1INB
  N35: Part10.D6_PWM, MD03A4.M1EN
  N36: Part10.D7_PWM, MD03A4.M1PWM
  N37: Part10.D29, R9.Pin_0, S5.pin_5
  N38: Part10.D30, S4.2, R11.Pin_0
  N39: Part10.D31, S3.2, R10.Pin_0
  N40: Part10.D32, R12.Pin_0, S5.pin_3
  N41: Part10.D33, R13.Pin_0, S5.pin_2
  N42: Part10.D34, R14.Pin_0, S5.pin_4
  N43: Part10.D35, R8.Pin_0, S5.pin_6
  N44: Power_supply_(19_V_16_A).GND, MD03A4.GND#131
  VCC: Power_supply_(19_V_16_A).VCC, MD03A4.VIN
  N45: R1.Pin_0, C5.1, Thermistor1.pin_0, Part5.AIN0
  N46: R2.Pin_0, C6.1, Part5.AIN3
  N47: R3.Pin_0, C4.1, Thermistor2.pin_0, Part5.AIN1
  N48: R4.Pin_0, C3.1, Thermistor3.pin_0, Part5.AIN2

custom parts:
  Adafruit LM4040 Voltage Reference: How good is your multimeter really? Or maybe your analog converter needs a good reference? Or lets say you want to test your microcontroller's conversion accuracy & precision. If only you had a dependable, high precision, rock-solid voltage reference. Now you know why we made this very cute and useful little breakout board. It has two very high precision shunt-type voltage references with 750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
  Adafruit 1.44 inch TFT Breakout: This lovely little display breakout is the best way to add a small, colorful and bright display to any project. Since the display uses 4-wire SPI to communicate and has its own pixel-addressable frame buffer, it can be used with every kind of microcontroller. Even a very small one with low memory and few pins available! The 1.44" display has 128x128 color pixels. Unlike the low cost "Nokia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
  OLED Monochrome 128x64 1.3 inch: These displays are small, only about 1.3" diagonal, but very readable due to the high contrast of an OLED display. This display is made of 128x64 individual white OLED pixels, each one is turned on or off by the controller chip. Because the display makes its own light, no backlight is required. This reduces the power required to run the OLED and is why the display has such high contrast; we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
  DRV8834: DRV8834 Low-Voltage Stepper Motor Driver Carrier.
  Pololu VNH5019 v8: The Pololu dual high-power motor driver carrier for the VNH2SP30 motor driver integrated circuits from ST. http://www.pololu.com/catalog/product/708
  Adafruit ADS1115 16Bit I2C ADC: For microcontrollers without an analog-to-digital converter or when you want a higher-precision ADC, the ADS1115 provides 16-bit precision at 860 samples/second over I2C. The chip can be configured as 4 single-ended input channels, or two differential channels. As a nice bonus, it even includes a programmable gain amplifier, up to x16, to help boost up smaller single/differential signals to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
  JOYSTICK_10mm_2: Small 5-way tactile joystick, 10MM
